# Fritzing sketch Sketch (saved by Fritzing 1.0.2b)
circuit board: 8.46667cm x 5.64444cm
stripboards: 1

parts:
  Pico_H4 = Raspberry Pi Pico H
  GY-NEO6MV7 = GY-NEO6MV2
  SPI2 = MicroSD Card Module
  Back_(2) = HC-SR04 Ultrasonic Distance Sensor
  Left_(3) = HC-SR04 Ultrasonic Distance Sensor
  3x_AAA = Battery Holders [package=battery-aa]
  READY = LED - 5mm [color="Green (555nm)" current=0.030A package="5 mm [THT]"]
  RUNNING = LED - 5mm [color="Green (555nm)" current=0.030A package="5 mm [THT]"]
  BATTERY = LED - 5mm [color="Red (633nm)" current=0.030A package="5 mm [THT]"]
  ERROR = LED - 5mm [color="Red (633nm)" current=0.030A package="5 mm [THT]"]
  Right_(1) = HC-SR04 Ultrasonic Distance Sensor
  U1 = SWITCH_SPDT [package=kps-1290]
  S1 = Pushbutton [package="[THT]"]
  200Ω = Resistor [tolerance=±1% resistance=220 power=0.25W package=THT]
  R7 = Resistor [tolerance=±1% power=0.25W resistance=330 package=THT]
  R4 = Resistor [tolerance=±1% power=0.25W resistance=100 package=THT]
  R10 = Resistor [tolerance=±1% power=0.25W resistance=100 package=THT]
  R9 = Resistor [tolerance=±1% power=0.25W resistance=100 package=THT]
  R8 = Resistor [tolerance=±1% power=0.25W resistance=100 package=THT]
  R6 = Resistor [tolerance=±1% power=0.25W resistance=1k package=THT]

nets:
  N1: Pico_H4.VSYS, U1.O, 200Ω.Pin_1
  GND: Pico_H4.GND, GY-NEO6MV7.GND, SPI2.GND, Back_(2).GND, Left_(3).GND, 3x_AAA.-, 3x_AAA.+, READY.anode, RUNNING.anode, BATTERY.anode, ERROR.anode, Right_(1).GND, U1.P, R7.Pin_0, R6.Pin_1
  VCC: Pico_H4.3V3, GY-NEO6MV7.Vcc, SPI2.VCC, Back_(2).VCC, Left_(3).VCC, Right_(1).VCC, S1.Pin_3, S1.Pin_4
  N2: Pico_H4.GP28_A2, 200Ω.Pin_0, R7.Pin_1
  N3: Pico_H4.GP27_A1, R4.Pin_0
  N4: Pico_H4.GP26_A0, R10.Pin_0
  N5: Pico_H4.GP22, R9.Pin_0
  N6: Pico_H4.GP21, R8.Pin_0
  N7: Pico_H4.GP19, Back_(2).ECHO
  N8: Pico_H4.GP18, Back_(2).TRIG
  N9: Pico_H4.GP17, GY-NEO6MV7.Tx
  N10: Pico_H4.GP16, GY-NEO6MV7.Rx
  N11: Pico_H4.GP13, SPI2.CS
  N12: Pico_H4.GP12, SPI2.MISO
  N13: Pico_H4.GP11, SPI2.MOSI
  N14: Pico_H4.GP10, SPI2.SCK
  N15: Pico_H4.GP9, Right_(1).ECHO
  N16: Pico_H4.GP8, Right_(1).TRIG
  N17: Pico_H4.GP5, S1.Pin_1, S1.Pin_2, R6.Pin_0
  N18: Pico_H4.GP3, Left_(3).ECHO
  N19: Pico_H4.GP2, Left_(3).TRIG
  N20: READY.cathode, R8.Pin_1
  N21: RUNNING.cathode, R9.Pin_1
  N22: BATTERY.cathode, R4.Pin_1
  N23: ERROR.cathode, R10.Pin_1

custom parts:
  Raspberry Pi Pico H: Raspberry Pi Pico H. Based around the RP2040 microcontroller the Pico H is a low cost microcontroller device bringing Raspberry Pi quality, cost, and easy of use to the microcontroller space.
  GY-NEO6MV2: Description: Module GPS , type GY-NEO6MV2, pour arduino et autres micro-contrôleurs. Caractéristiques De type GY-NEO6MV2 Alimentation 3V-5V Avec Flight Control EEPROM MWC Antenne large céramique, fort signal, 25 x 25 mm Paramètres de configuration sauvegardés en EEPROM Avec batterie de backup de données LED témoin de signal Module miniaturisé 25 x 35 mm Trou de fixation de 3mm Baud rate par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
  MicroSD Card Module: A common microSD card module.
